# Fritzing sketch BinocularsHUD (saved by Fritzing 0.9.2b)
breadboards: 1

parts:
  PCB2 = RTC_DS1302_module
  Part1 = Arduino Due (Rev2b)
  Part2 = OLED Monochrome 128x64 0.96 inch [part_number=326]
  Part3 = 9 Degrees of Freedom - Sensor Stick

nets:
  VCC: PCB2.VCC, Part1.IOREF, Part2.3.3V, Part3.VCC
  GND: PCB2.GND, Part1.GND, Part2.GND, Part3.GND
  N1: PCB2.RST, Part1.D5_PWM
  N2: PCB2.DAT, Part1.D6_PWM
  N3: PCB2.CLK, Part1.D7_PWM
  N4: Part1.D18/TX1, Part3.RX
  N5: Part1.D19/RX1, Part3.TX
  N6: Part1.D8_PWM, Part2.RESET
  N7: Part1.D9_PWM, Part2.DC_SA0
  N8: Part1.D10_PWM/SS0, Part2.CS
  N9: Part1.D11_PWM, Part2.MOSI_SDA
  N10: Part1.D13_PWM, Part2.SCLK_SCK

custom parts:
  RTC_DS1302_module: Arduino module DS1302 SPI Real Time Clock
  OLED Monochrome 128x64 0.96 inch: These displays are small, only about 1" diameter, but very readable due to the high contrast of an OLED display. This display is made of 128x64 individual white OLED pixels, each one is turned on or off by the controller chip. Because the display makes its own light, no backlight is required. This reduces the power required to run the OLED and is why the display has such high contrast; we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
  9 Degrees of Freedom - Sensor Stick: Description: The 9DOF Sensor stick is a very small sensor board with 9 degrees of freedom. It includes the ADXL345 accelerometer, the HMC5883L magnetometer, and the ITG-3200 gyro. The 'stick' has a simple I2C interface and a mounting hole for attaching it to your project. Also, the board is a mere 0.036" thick (0.093" overall), allowing it to be easily mounted in just about any application.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
